// Logisim project 1.circ as structural Verilog: 1 circuit, main circuit main
module main (
  input  [7:0] in_1,
  output [2:0] out_2
);

  wire [7:0] _0_out, _8_out;

  // Probe on in_1
  and _0 (_0_out[0], ~in_1[7], ~in_1[6], ~in_1[5], ~in_1[4], ~in_1[3], ~in_1[2], ~in_1[1], ~in_1[0]);  // AND_Gate
  and _1 (_0_out[1], ~in_1[7], ~in_1[6], ~in_1[5], ~in_1[4], ~in_1[3], ~in_1[2], ~in_1[1], in_1[0]);  // AND_Gate
  and _2 (_0_out[2], ~in_1[7], ~in_1[6], ~in_1[5], ~in_1[4], ~in_1[3], ~in_1[2], in_1[1], ~in_1[0]);  // AND_Gate
  and _3 (_0_out[3], ~in_1[7], ~in_1[6], ~in_1[5], ~in_1[4], ~in_1[3], ~in_1[2], in_1[1], in_1[0]);  // AND_Gate
  and _4 (_0_out[4], ~in_1[7], ~in_1[6], ~in_1[5], ~in_1[4], ~in_1[3], in_1[2], ~in_1[1], ~in_1[0]);  // AND_Gate
  and _5 (_0_out[5], ~in_1[7], ~in_1[6], ~in_1[5], ~in_1[4], ~in_1[3], in_1[2], ~in_1[1], in_1[0]);  // AND_Gate
  and _6 (_0_out[6], ~in_1[7], ~in_1[6], ~in_1[5], ~in_1[4], ~in_1[3], in_1[2], in_1[1], ~in_1[0]);  // AND_Gate
  and _7 (_0_out[7], ~in_1[7], ~in_1[6], ~in_1[5], ~in_1[4], ~in_1[3], in_1[2], in_1[1], in_1[0]);  // AND_Gate
  and _8 (_8_out[0], ~in_1[7], ~in_1[6], ~in_1[5], ~in_1[4], in_1[3], ~in_1[2], ~in_1[1], ~in_1[0]);  // AND_Gate
  and _9 (_8_out[1], ~in_1[7], ~in_1[6], ~in_1[5], ~in_1[4], in_1[3], ~in_1[2], in_1[1], ~in_1[0]);  // AND_Gate
  and _10 (_8_out[2], ~in_1[7], ~in_1[6], ~in_1[5], ~in_1[4], in_1[3], in_1[2], ~in_1[1], ~in_1[0]);  // AND_Gate
  and _11 (_8_out[3], ~in_1[7], ~in_1[6], ~in_1[5], ~in_1[4], in_1[3], in_1[2], in_1[1], ~in_1[0]);  // AND_Gate
  and _12 (_8_out[4], ~in_1[7], ~in_1[6], ~in_1[5], in_1[4]);  // AND_Gate
  and _13 (_8_out[5], ~in_1[7], in_1[6], in_1[5], ~in_1[4]);  // AND_Gate
  and _14 (_8_out[6], in_1[7], ~in_1[6], in_1[5], ~in_1[4]);  // AND_Gate
  and _15 (_8_out[7], in_1[7], in_1[6], in_1[5], ~in_1[4]);  // AND_Gate
  or O2 (out_2[2], _0_out[2], _0_out[5], _0_out[6], _8_out[0], _8_out[1], _8_out[2], _8_out[5], _8_out[6]);
  or O1 (out_2[1], _0_out[1], _0_out[2], _0_out[3], _0_out[4], _0_out[5], _8_out[1], _8_out[3], _8_out[4], _8_out[5], _8_out[6], _8_out[7]);
  or O0 (out_2[0], _0_out[0], _0_out[4], _0_out[5], _8_out[1], _8_out[2], _8_out[3], _8_out[5], _8_out[7]);
  // Probe on out_2
endmodule
