// Logisim project 2.circ as structural Verilog: 1 circuit, main circuit main
module main (
  input  [3:0] in_1,
  output [1:0] out_2
);

  ROM #(.addrWidth(4), .dataWidth(2)) rom_1 (.addr(in_1), .data(out_2));  // open: sel

  // Notes on the sheet:
  //   contents of rom_1 (hex, n*v repeats v):
  //   3 2 1 3 2 1 3 3 3 0 3 0 2 0 3
endmodule
