// Logisim project 3.circ as structural Verilog: 1 circuit, main circuit main
module main (
  input  [7:0] in_1,
  output [2:0] out_2
);

  ROM #(.dataWidth(3)) rom_1 (.addr(in_1), .data(out_2));  // open: sel

  // Notes on the sheet:
  //   contents of rom_1 (hex, n*v repeats v):
  //   1 2 6 2 3 7 4 0 4 0 7 0 5 0 3 0 16*2 64*0 16*7 48*0 16*6 48*0 16*3
endmodule
