// Logisim project Lab 1 Given.circ as structural Verilog: 5 circuits, main circuit Main
module Main (
);

  wire Clock;
  wire [1:0] ROMSimpleCombinationalOutput;
  wire [2:0] CombinationalOutput, ROMCombinationalOutput;
  wire [3:0] SimpleInput;
  wire [7:0] Input;

  Combinational_Input combinational_input_1 (
    .In7(Input[7]), .In6(Input[6]), .In5(Input[5]), .In4(Input[4]), .In3(Input[3]), .In2(Input[2]),
    .In1(Input[1]), .In0(Input[0]), .Clock(Clock));
  Simple_Combinational_Input simple_combinational_input_1 (
    .In3(SimpleInput[3]), .In2(SimpleInput[2]), .In1(SimpleInput[1]), .In0(SimpleInput[0]), .Clock(Clock));
  Clock clock_1 (.out(Clock));
  _1_main main_1 (.in_1(Input), .out_2(CombinationalOutput));
  _2_main main_2 (.in_1(SimpleInput), .out_2(ROMSimpleCombinationalOutput));
  _3_main main_3 (.in_1(Input), .out_2(ROMCombinationalOutput));
  // Probe on Input
  // Probe on SimpleInput
  // Probe on CombinationalOutput
  // Probe on ROMSimpleCombinationalOutput
  // Probe on ROMCombinationalOutput
endmodule

module Combinational_Input (
  input  Clock,
  output In7,
  output In6,
  output In5,
  output In4,
  output In3,
  output In2,
  output In1,
  output In0
);

  Counter #(.ongoal("stay")) counter_1 (
    .count(1'b1), .Q({In7, In6, In5, In4, In3, In2, In1, In0}), .clk(Clock));  // open: load, D, carry, clr
endmodule

module Simple_Combinational_Input (
  input  Clock,
  output In3,
  output In2,
  output In1,
  output In0
);

  Counter #(.width(4), .max('hf), .ongoal("stay")) counter_1 (
    .count(1'b1), .Q({In3, In2, In1, In0}), .clk(Clock));  // open: load, D, carry, clr
endmodule

module ROM_XOR (
  input  X,
  input  Y,
  output X_XOR_Y
);

  ROM #(.addrWidth(2), .dataWidth(1)) rom_1 (.addr({X, Y}), .data(X_XOR_Y));  // open: sel

  // Notes on the sheet:
  //   contents of rom_1 (hex, n*v repeats v):
  //   0 1 1
endmodule

module ROM_Sequential (
  input  X,
  input  Clock,
  output [1:0] Out
);

  wire [1:1] register_1_q;
  wire [2:0] rom_1_data;

  ROM #(.addrWidth(2), .dataWidth(3)) rom_1 (.addr({register_1_q[1], X}), .data(rom_1_data));  // open: sel
  Register #(.width(3)) register_1 (.D(rom_1_data), .Q({register_1_q[1], Out}), .clk(Clock));  // open: en, clr

  // Notes on the sheet:
  //   contents of rom_1 (hex, n*v repeats v):
  //   1 5 7 3
endmodule
