// Logisim project ALU control.circ as structural Verilog: 1 circuit, main circuit main
module main (
  input  [5:0] Instruction__5_0,
  input  [2:0] ALUOp,
  output [2:0] ALUCtl
);

  wire ADD_out, OR_out, SLT_out, SUB_out, XOR_out;
  wire [2:0] or_4_out;

  and ADD (ADD_out, ~Instruction__5_0[0], ~Instruction__5_0[1], ~Instruction__5_0[2], ~Instruction__5_0[3], ~Instruction__5_0[4], Instruction__5_0[5]);  // AND_Gate
  // AND_Gate AND has open pins: in0=Instruction__5_0[0], in1=Instruction__5_0[1], in2=Instruction__5_0[2], in3=Instruction__5_0[3], in4=Instruction__5_0[4], in5=Instruction__5_0[5], out=open
  and OR (OR_out, Instruction__5_0[0], ~Instruction__5_0[1], Instruction__5_0[2], ~Instruction__5_0[3], ~Instruction__5_0[4], Instruction__5_0[5]);  // AND_Gate
  and SUB (SUB_out, ~Instruction__5_0[0], Instruction__5_0[1], ~Instruction__5_0[2], ~Instruction__5_0[3], ~Instruction__5_0[4], Instruction__5_0[5]);  // AND_Gate
  and SLT (SLT_out, ~Instruction__5_0[0], Instruction__5_0[1], ~Instruction__5_0[2], Instruction__5_0[3], ~Instruction__5_0[4], Instruction__5_0[5]);  // AND_Gate
  and XOR (XOR_out, ~Instruction__5_0[0], Instruction__5_0[1], Instruction__5_0[2], ~Instruction__5_0[3], ~Instruction__5_0[4], Instruction__5_0[5]);  // AND_Gate
  // AND_Gate JR has open pins: in0=Instruction__5_0[0], in1=Instruction__5_0[1], in2=Instruction__5_0[2], in3=Instruction__5_0[3], in4=Instruction__5_0[4], in5=Instruction__5_0[5], out=open
  or or_2 (or_4_out[2], SLT_out, XOR_out);
  or or_3 (or_4_out[1], OR_out, SUB_out);
  or or_4 (or_4_out[0], ADD_out, SUB_out, XOR_out);
  Multiplexer #(.select(3), .width(3)) multiplexer_1 (
    .in0(3'b001), .in1(3'b011), .in2(or_4_out), .in3(3'b010), .in4(3'b000), .out(ALUCtl), .sel(ALUOp));  // open: in5, in6, in7, en

  // Other names for the same wires on the sheet: FUNCT[5:0] = Instruction__5_0
endmodule
