// Logisim project Control Unit.circ as structural Verilog: 1 circuit, main circuit main
module main (
  input  [5:0] Instruction__31_26,
  input  [5:0] FUNCT,
  output Outputs,
  output out_4,
  output out_5,
  output out_6,
  output [2:0] out_7,
  output out_8,
  output out_9,
  output out_10,
  output out_11,
  output out_12,
  output out_13
);

  wire ADDI_out, J_out, JR_Func_out, JR_out, ORI_out;

  and R (Outputs, ~Instruction__31_26[0], ~Instruction__31_26[1], ~Instruction__31_26[2], ~Instruction__31_26[3], ~Instruction__31_26[4], ~Instruction__31_26[5]);  // AND_Gate
  and lw (out_5, Instruction__31_26[0], Instruction__31_26[1], ~Instruction__31_26[2], ~Instruction__31_26[3], ~Instruction__31_26[4], Instruction__31_26[5]);  // AND_Gate
  and sw (out_8, Instruction__31_26[0], Instruction__31_26[1], ~Instruction__31_26[2], Instruction__31_26[3], ~Instruction__31_26[4], Instruction__31_26[5]);  // AND_Gate
  and beq (out_4, ~Instruction__31_26[0], ~Instruction__31_26[1], Instruction__31_26[2], ~Instruction__31_26[3], ~Instruction__31_26[4], ~Instruction__31_26[5]);  // AND_Gate
  and ADDI (ADDI_out, ~Instruction__31_26[0], ~Instruction__31_26[1], ~Instruction__31_26[2], Instruction__31_26[3], ~Instruction__31_26[4], ~Instruction__31_26[5]);  // AND_Gate
  and ANDI (out_7[2], ~Instruction__31_26[0], ~Instruction__31_26[1], Instruction__31_26[2], Instruction__31_26[3], ~Instruction__31_26[4], ~Instruction__31_26[5]);  // AND_Gate
  and ORI (ORI_out, Instruction__31_26[0], ~Instruction__31_26[1], Instruction__31_26[2], Instruction__31_26[3], ~Instruction__31_26[4], ~Instruction__31_26[5]);  // AND_Gate
  and J (J_out, ~Instruction__31_26[0], Instruction__31_26[1], ~Instruction__31_26[2], ~Instruction__31_26[3], ~Instruction__31_26[4], ~Instruction__31_26[5]);  // AND_Gate
  and JAL (out_12, Instruction__31_26[0], Instruction__31_26[1], ~Instruction__31_26[2], ~Instruction__31_26[3], ~Instruction__31_26[4], ~Instruction__31_26[5]);  // AND_Gate
  and JR (JR_out, ~Instruction__31_26[0], ~Instruction__31_26[1], ~Instruction__31_26[2], ~Instruction__31_26[3], ~Instruction__31_26[4], ~Instruction__31_26[5]);  // AND_Gate
  and JR_Func (JR_Func_out, ~FUNCT[0], ~FUNCT[1], ~FUNCT[2], FUNCT[3], ~FUNCT[4], ~FUNCT[5]);  // AND_Gate
  or or_1 (out_9, out_5, out_8, ADDI_out, out_7[2], ORI_out);
  or or_2 (out_10, Outputs, out_5, ADDI_out, out_7[2], ORI_out, out_12);
  or or_3 (out_7[1], Outputs, ORI_out);
  or or_4 (out_7[0], out_4, ORI_out);
  or or_5 (out_11, J_out, out_12);
  and and_1 (out_13, JR_out, JR_Func_out);

  assign out_6 = out_5;

  // Other names for the same wires on the sheet: ALUOp[2:0] = out_7; ALUOp0 = out_7[0]; ALUOp1 = out_7[1];
  //   ALUOp2 = out_7[2]; ALUSrc = out_9; Branch = out_4; Instruction[5:0] = Instruction__31_26; JAL = out_12;
  //   JR = out_13; Jump = out_11; MemRead = out_5; MemtoReg = out_5; MemWrite = out_8; RegDst = Outputs;
  //   RegWrite = out_10

  // Notes on the sheet:
  //   RegDst (1): rd signal
  //   Branch (1): branch signal
  //   MemRead (1): read enable signal
  //   ALUOp (2): ALU Control signal
  //   Jump (1): high on J
  //   JAL (1): high on JAL
  //   JR (1): high on JR
  //   MemWrite (1): Write enable signal
  //   ALUSrc (1): 2nd operand, =0 for rt, =1 for immediate value
  //   RegWrite (1): enable write to one reg
  //   MemtoReg (1): =0 from ALUOutput (R-type), =1 from MDR (lw)
  //   ALUOp
  //   000 Add for L/S
  //   001 Sub for beq
  //   010 from FUNCT field
  //   011 Or
  //   100 And
endmodule
