// Logisim project Lab 2 Given.circ as structural Verilog: 4 circuits, main circuit Main
module Main (
);

  wire alu_1_zero, ALUSrc, and_1_out, Branch, CLK, JAL, JR, Jump, MemRead, MemtoReg, MemWrite, RegDst,
       RegWrite;
  wire [2:0] ALUCtl, ALUOp;
  wire [4:0] Inst_20_16, Inst_25_21, multiplexer_1_out, WrAddr;
  wire [5:0] Inst_5_0, Inst_31_26;
  wire [7:0] PC;
  wire [15:6] Inst_15_0;
  wire [31:0] A, adder_2_out, ALUresult, B, main_1_p1, main_1_p2, main_4_out_2, main_5_out_2,
       main_7_read_data, MemData, multiplexer_4_out, multiplexer_5_out, multiplexer_7_out, PC_4, WrData;

  // Probe on main_1_p1
  // PC_main main_1: pin names not known; wires that end beside it: main_1_p1, {main_1_p2[31:10], PC, main_1_p2[1:0]}
  // Probe on {main_1_p2[31:10], PC, main_1_p2[1:0]}
  Adder #(.width(32)) adder_1 (.a({main_1_p2[31:10], PC, main_1_p2[1:0]}), .b(32'h4), .out(PC_4));  // open: cin, cout
  // Probe on Inst_31_26
  Instruction_Memory_main main_2 (
    .Read_address(PC), .Instruction({Inst_31_26, Inst_25_21, Inst_20_16, Inst_15_0, Inst_5_0}));
  Control_Unit_main main_3 (
    .Instruction__31_26(Inst_31_26), .Outputs(RegDst), .out_4(Branch), .out_5(MemRead), .out_6(MemtoReg),
    .out_7(ALUOp), .out_8(MemWrite), .out_9(ALUSrc), .out_10(RegWrite), .FUNCT(Inst_5_0), .out_11(Jump),
    .out_12(JAL), .out_13(JR));
  Sign_extension_main main_4 (.in_1({Inst_15_0, Inst_5_0}), .out_2(main_4_out_2));
  Multiplexer #(.width(5)) multiplexer_1 (
    .in0(Inst_20_16), .in1(Inst_15_0[15:11]), .out(multiplexer_1_out), .sel(RegDst));  // open: en
  Multiplexer #(.width(5)) multiplexer_2 (
    .in0(multiplexer_1_out), .in1({5{1'b1}}), .out(WrAddr), .sel(JAL));  // open: en
  Register_File register_file_1 (
    .WrAddr(WrAddr), .WrData(WrData), .WrReg(RegWrite), .RdAddr1(Inst_25_21), .RdAddr2(Inst_20_16),
    .RdData1(A), .RdData2(MemData), .Clock(CLK));
  // Probe on Inst_25_21
  // Probe on Inst_20_16
  Multiplexer #(.width(32)) multiplexer_3 (.in0(MemData), .in1(main_4_out_2), .out(B), .sel(ALUSrc));  // open: en
  Adder #(.width(32)) adder_2 (.a(PC_4), .b(main_5_out_2), .out(adder_2_out));  // open: cin, cout
  Left_shift_2_main main_5 (.in_1(main_4_out_2), .out_2(main_5_out_2));
  ALU alu_1 (
    .ALUCtl(ALUCtl), .A(A), .B(B), .ALUResult(ALUresult), .Zero(alu_1_zero), .Shamt({5{1'b0}}));  // open: Overflow
  Multiplexer #(.width(32)) multiplexer_4 (
    .in0(PC_4), .in1(adder_2_out), .out(multiplexer_4_out), .sel(and_1_out));  // open: en
  and and_1 (and_1_out, Branch, alu_1_zero);
  ALU_control_main main_6 (.Instruction__5_0(Inst_5_0), .ALUCtl(ALUCtl), .ALUOp(ALUOp));
  Multiplexer #(.width(32)) multiplexer_5 (
    .in0(multiplexer_4_out), .in1({4'b0000, Inst_25_21, Inst_20_16, Inst_15_0, Inst_5_0, 2'b00}),
    .out(multiplexer_5_out), .sel(Jump));  // open: en
  Data_Memory_main main_7 (
    .Address(ALUresult[9:2]), .Write_Data(MemData), .Read_Data(main_7_read_data), .MemWrite(MemWrite),
    .CLK(CLK), .MemRead(MemRead));
  // Probe on ALUCtl
  // Probe on A
  // Probe on B
  // Probe on ALUresult
  // Probe on {Inst_31_26, Inst_25_21, Inst_20_16, Inst_15_0, Inst_5_0}
  // Probe on {4'b0000, Inst_25_21, Inst_20_16, Inst_15_0, Inst_5_0, 2'b00}
  Multiplexer #(.width(32)) multiplexer_6 (.in0(multiplexer_5_out), .in1(A), .out(main_1_p1), .sel(JR));  // open: en
  Multiplexer #(.width(32)) multiplexer_7 (
    .in0(ALUresult), .in1(main_7_read_data), .out(multiplexer_7_out), .sel(MemtoReg));  // open: en
  Multiplexer #(.width(32)) multiplexer_8 (.in0(multiplexer_7_out), .in1(PC_4), .out(WrData), .sel(JAL));  // open: en
  Clock clock_1 (.out(CLK));
  // Probe on PC
  // Probe on Branch
  // Probe on Jump
  // Probe on JAL
  // Probe on JR
  // Probe on RegWrite
  // Probe on WrAddr
  // Probe on WrData
  // Probe on MemWrite
  // Probe on MemData

  // Other names for the same wires on the sheet: Instruction[31:0] = {Inst_31_26, Inst_25_21, Inst_20_16, Inst_15_0, Inst_5_0};
  //   JRaddr[31:0] = A; Inst_15_0[5:0] = Inst_5_0; JumpAddr[27:2] = {Inst_25_21, Inst_20_16, Inst_15_0, Inst_5_0};
  //   Inst_15_11[4:0] = Inst_15_0[15:11]

  // Notes on the sheet:
  //   rs
  //   rt
  //   JAL
  //   select 31
  //   MUX
  //   PC+4
  //   Branch
  //   MUX
  //   Handles jump for
  //   J and JAL
  //   Jump
  //   MUX
  //   JR
  //   MUX
  //   JAL
  //   Link
  //   MUX
endmodule

module ALU (
  input  [2:0] ALUCtl,
  input  [31:0] A,
  input  [31:0] B,
  input  [4:0] Shamt,
  output [31:0] ALUResult,
  output Zero,
  output Overflow
);

  wire comparator_1_lt, comparator_2_lt, comparator_3_eq, comparator_4_eq, or_2_out;
  wire [31:0] ADD, AND, NOR, OR, SLL, SLT, SLTU, SRL, SUB, XOR;

  // Probe on ALUCtl
  assign NOR = ~(A | B);  // NOR_Gate nor_1, 32 bits wide
  Adder #(.width(32)) adder_1 (.a(A), .b(B), .out(ADD));  // open: cin, cout
  Subtractor #(.width(32)) subtractor_1 (.a(A), .b(B), .out(SUB));  // open: bin, bout
  assign AND = A & B;  // AND_Gate and_1, 32 bits wide
  assign OR = A | B;  // OR_Gate or_1, 32 bits wide
  assign XOR = A ^ B;  // XOR_Gate xor_1, 32 bits wide
  Comparator #(.width(32)) comparator_1 (.a(A), .b(B), .lt(comparator_1_lt));  // open: gt, eq
  assign SLT = {{31{1'b0}}, comparator_1_lt};  // Bit_Extender bit_extender_1
  Shifter #(.width(32)) shifter_1 (.in(B), .\dist (Shamt), .out(SLL));
  Shifter #(.width(32), .shift("lr")) shifter_2 (.in(B), .\dist (Shamt), .out(SRL));
  Comparator #(.width(32), .mode("unsigned")) comparator_2 (.a(A), .b(B), .lt(comparator_2_lt));  // open: gt, eq
  assign SLTU = {{31{1'b0}}, comparator_2_lt};  // Bit_Extender bit_extender_2
  Multiplexer #(.select(3), .width(32), .enable("false")) multiplexer_1 (
    .in0(AND), .in1(ADD), .in2(OR), .in3(SUB), .in4(SLT), .in5(XOR), .out(ALUResult), .sel(ALUCtl));  // open: in6, in7
  Comparator #(.width(3)) comparator_3 (.a(3'b001), .b(ALUCtl), .eq(comparator_3_eq));  // open: gt, lt
  Comparator #(.width(3)) comparator_4 (.a(ALUCtl), .b(3'b011), .eq(comparator_4_eq));  // open: gt, lt
  Overflow_Unit overflow_unit_1 (
    .Add(comparator_3_eq), .Sub(comparator_4_eq), .ASign(A[31]), .BSign(B[31]), .ResultSign(ALUResult[31]),
    .Overflow(Overflow));
  or or_2 (or_2_out, ALUResult[0], ALUResult[1], ALUResult[2], ALUResult[3], ALUResult[4], ALUResult[5], ALUResult[6], ALUResult[7], ALUResult[8], ALUResult[9], ALUResult[10], ALUResult[11], ALUResult[12], ALUResult[13], ALUResult[14], ALUResult[15], ALUResult[16], ALUResult[17], ALUResult[18], ALUResult[19], ALUResult[20], ALUResult[21], ALUResult[22], ALUResult[23], ALUResult[24], ALUResult[25], ALUResult[26], ALUResult[27], ALUResult[28], ALUResult[29], ALUResult[30], ALUResult[31]);
  not not_1 (Zero, or_2_out);

  // Other names for the same wires on the sheet: ASign = A[31]; ResultSign = ALUResult[31]; BSign = B[31]

  // Notes on the sheet:
  //   ALUCtl for ADD for top port
  //   ALUCtl for SUB for second port
endmodule

module Register_File (
  input  [4:0] WrAddr,
  input  [31:0] WrData,
  input  WrReg,
  input  [4:0] RdAddr1,
  input  [4:0] RdAddr2,
  input  Clock,
  output [31:0] RdData1,
  output [31:0] RdData2
);

  wire WrReg0, WrReg1, WrReg2, WrReg3, WrReg4, WrReg5, WrReg6, WrReg7, WrReg8, WrReg9, WrReg10, WrReg11,
       WrReg12, WrReg13, WrReg14, WrReg15, WrReg16, WrReg17, WrReg18, WrReg19, WrReg20, WrReg21, WrReg22,
       WrReg23, WrReg24, WrReg25, WrReg26, WrReg27, WrReg28, WrReg29, WrReg30, WrReg31;
  wire [31:0] RegData1, RegData2, RegData3, RegData4, RegData5, RegData6, RegData7, RegData8, RegData9,
       RegData10, RegData11, RegData12, RegData13, RegData14, RegData15, RegData16, RegData17, RegData18,
       RegData19, RegData20, RegData21, RegData22, RegData23, RegData24, RegData25, RegData26, RegData27,
       RegData28, RegData29, RegData30, RegData31;

  Demultiplexer #(.select(5), .enable("false")) demultiplexer_1 (
    .out0(WrReg0), .out1(WrReg1), .out2(WrReg2), .out3(WrReg3), .out4(WrReg4), .out5(WrReg5), .out6(WrReg6),
    .out7(WrReg7), .out8(WrReg8), .out9(WrReg9), .out10(WrReg10), .out11(WrReg11), .out12(WrReg12),
    .out13(WrReg13), .out14(WrReg14), .out15(WrReg15), .out16(WrReg16), .out17(WrReg17), .out18(WrReg18),
    .out19(WrReg19), .out20(WrReg20), .out21(WrReg21), .out22(WrReg22), .out23(WrReg23), .out24(WrReg24),
    .out25(WrReg25), .out26(WrReg26), .out27(WrReg27), .out28(WrReg28), .out29(WrReg29), .out30(WrReg30),
    .out31(WrReg31), .in(WrReg), .sel(WrAddr));
  // Probe on RegData4
  Register #(.width(32)) Reg4 (.D(WrData), .en(WrReg4), .Q(RegData4), .clk(Clock));  // open: clr
  // Probe on RegData8
  Register #(.width(32)) Reg8 (.D(WrData), .en(WrReg8), .Q(RegData8), .clk(Clock));  // open: clr
  // Probe on RegData12
  Register #(.width(32)) Reg12 (.D(WrData), .en(WrReg12), .Q(RegData12), .clk(Clock));  // open: clr
  // Probe on RegData16
  Register #(.width(32)) Reg16 (.D(WrData), .en(WrReg16), .Q(RegData16), .clk(Clock));  // open: clr
  // Probe on RegData20
  Register #(.width(32)) Reg20 (.D(WrData), .en(WrReg20), .Q(RegData20), .clk(Clock));  // open: clr
  // Probe on RegData24
  Register #(.width(32)) Reg24 (.D(WrData), .en(WrReg24), .Q(RegData24), .clk(Clock));  // open: clr
  // Probe on RegData28
  Register #(.width(32)) Reg28 (.D(WrData), .en(WrReg28), .Q(RegData28), .clk(Clock));  // open: clr
  Register #(.width(32)) Reg1 (.D(WrData), .en(WrReg1), .Q(RegData1), .clk(Clock));  // open: clr
  Register #(.width(32)) Reg5 (.D(WrData), .en(WrReg5), .Q(RegData5), .clk(Clock));  // open: clr
  Register #(.width(32)) Reg9 (.D(WrData), .en(WrReg9), .Q(RegData9), .clk(Clock));  // open: clr
  Register #(.width(32)) Reg13 (.D(WrData), .en(WrReg13), .Q(RegData13), .clk(Clock));  // open: clr
  Register #(.width(32)) Reg17 (.D(WrData), .en(WrReg17), .Q(RegData17), .clk(Clock));  // open: clr
  Register #(.width(32)) Reg21 (.D(WrData), .en(WrReg21), .Q(RegData21), .clk(Clock));  // open: clr
  Register #(.width(32)) Reg25 (.D(WrData), .en(WrReg25), .Q(RegData25), .clk(Clock));  // open: clr
  Register #(.width(32)) Reg29 (.D(WrData), .en(WrReg29), .Q(RegData29), .clk(Clock));  // open: clr
  // Probe on RegData1
  // Probe on RegData5
  // Probe on RegData9
  // Probe on RegData13
  // Probe on RegData17
  // Probe on RegData21
  // Probe on RegData25
  // Probe on RegData29
  // Probe on RegData2
  Register #(.width(32)) Reg2 (.D(WrData), .en(WrReg2), .Q(RegData2), .clk(Clock));  // open: clr
  // Probe on RegData6
  Register #(.width(32)) Reg6 (.D(WrData), .en(WrReg6), .Q(RegData6), .clk(Clock));  // open: clr
  // Probe on RegData10
  Register #(.width(32)) Reg10 (.D(WrData), .en(WrReg10), .Q(RegData10), .clk(Clock));  // open: clr
  // Probe on RegData14
  Register #(.width(32)) Reg14 (.D(WrData), .en(WrReg14), .Q(RegData14), .clk(Clock));  // open: clr
  // Probe on RegData18
  Register #(.width(32)) Reg18 (.D(WrData), .en(WrReg18), .Q(RegData18), .clk(Clock));  // open: clr
  // Probe on RegData22
  Register #(.width(32)) Reg22 (.D(WrData), .en(WrReg22), .Q(RegData22), .clk(Clock));  // open: clr
  // Probe on RegData26
  Register #(.width(32)) Reg26 (.D(WrData), .en(WrReg26), .Q(RegData26), .clk(Clock));  // open: clr
  // Probe on RegData30
  Register #(.width(32)) Reg30 (.D(WrData), .en(WrReg30), .Q(RegData30), .clk(Clock));  // open: clr
  // Probe on RegData3
  Register #(.width(32)) Reg3 (.D(WrData), .en(WrReg3), .Q(RegData3), .clk(Clock));  // open: clr
  // Probe on RegData7
  Register #(.width(32)) Reg7 (.D(WrData), .en(WrReg7), .Q(RegData7), .clk(Clock));  // open: clr
  // Probe on RegData11
  Register #(.width(32)) Reg11 (.D(WrData), .en(WrReg11), .Q(RegData11), .clk(Clock));  // open: clr
  // Probe on RegData15
  Register #(.width(32)) Reg15 (.D(WrData), .en(WrReg15), .Q(RegData15), .clk(Clock));  // open: clr
  // Probe on RegData19
  Register #(.width(32)) Reg19 (.D(WrData), .en(WrReg19), .Q(RegData19), .clk(Clock));  // open: clr
  // Probe on RegData23
  Register #(.width(32)) Reg23 (.D(WrData), .en(WrReg23), .Q(RegData23), .clk(Clock));  // open: clr
  // Probe on RegData27
  Register #(.width(32)) Reg27 (.D(WrData), .en(WrReg27), .Q(RegData27), .clk(Clock));  // open: clr
  // Probe on RegData31
  Register #(.width(32)) Reg31 (.D(WrData), .en(WrReg31), .Q(RegData31), .clk(Clock));  // open: clr
  Multiplexer #(.select(5), .width(32), .enable("false")) multiplexer_1 (
    .in0({32{1'b0}}), .in1(RegData1), .in2(RegData2), .in3(RegData3), .in4(RegData4), .in5(RegData5),
    .in6(RegData6), .in7(RegData7), .in8(RegData8), .in9(RegData9), .in10(RegData10), .in11(RegData11),
    .in12(RegData12), .in13(RegData13), .in14(RegData14), .in15(RegData15), .in16(RegData16),
    .in17(RegData17), .in18(RegData18), .in19(RegData19), .in20(RegData20), .in21(RegData21),
    .in22(RegData22), .in23(RegData23), .in24(RegData24), .in25(RegData25), .in26(RegData26),
    .in27(RegData27), .in28(RegData28), .in29(RegData29), .in30(RegData30), .in31(RegData31), .out(RdData1),
    .sel(RdAddr1));
  Multiplexer #(.select(5), .width(32), .enable("false")) multiplexer_2 (
    .in0({32{1'b0}}), .in1(RegData1), .in2(RegData2), .in3(RegData3), .in4(RegData4), .in5(RegData5),
    .in6(RegData6), .in7(RegData7), .in8(RegData8), .in9(RegData9), .in10(RegData10), .in11(RegData11),
    .in12(RegData12), .in13(RegData13), .in14(RegData14), .in15(RegData15), .in16(RegData16),
    .in17(RegData17), .in18(RegData18), .in19(RegData19), .in20(RegData20), .in21(RegData21),
    .in22(RegData22), .in23(RegData23), .in24(RegData24), .in25(RegData25), .in26(RegData26),
    .in27(RegData27), .in28(RegData28), .in29(RegData29), .in30(RegData30), .in31(RegData31), .out(RdData2),
    .sel(RdAddr2));
endmodule

module Overflow_Unit (
  input  Add,
  input  Sub,
  input  ASign,
  input  BSign,
  input  ResultSign,
  output Overflow
);

  wire and_1_out, and_2_out, or_1_out, xnor_1_out, xor_1_out, xor_2_out;

  xnor xnor_1 (xnor_1_out, ASign, BSign);
  xor xor_1 (xor_1_out, ASign, BSign);
  and and_1 (and_1_out, xnor_1_out, Add);
  and and_2 (and_2_out, xor_1_out, Sub);
  or or_1 (or_1_out, and_1_out, and_2_out);
  xor xor_2 (xor_2_out, ResultSign, ASign);
  and and_3 (Overflow, or_1_out, xor_2_out);

  // Notes on the sheet:
  //   Overflow occurs when doing addition and sign(A) == sign(B) && sign(result) != sign(A)
  //   Or
  //   Overflow occurs when doing subtraction and sign(A) != sign(B) && sign(result) != sign(A)
endmodule
