// Logisim project Right shift 2.circ as structural Verilog: 1 circuit, main circuit main
module main (
  input  [7:0] in_1,
  output [7:0] out_2
);

  Shifter #(.shift("ar")) shifter_1 (.in(in_1), .\dist (3'b010), .out(out_2));
endmodule
