// Logisim project Control Unit.circ as structural Verilog: 1 circuit, main circuit main
module main (
  input  [5:0] Instruction__31_26,
  output Outputs,
  output out_3,
  output out_4,
  output out_5,
  output [1:0] out_6,
  output out_7,
  output out_8,
  output out_9
);

  and R (out_6[1], ~Instruction__31_26[0], ~Instruction__31_26[1], ~Instruction__31_26[2], ~Instruction__31_26[3], ~Instruction__31_26[4], ~Instruction__31_26[5]);  // AND_Gate
  and lw (out_4, Instruction__31_26[0], Instruction__31_26[1], ~Instruction__31_26[2], ~Instruction__31_26[3], ~Instruction__31_26[4], Instruction__31_26[5]);  // AND_Gate
  and sw (out_7, Instruction__31_26[0], Instruction__31_26[1], ~Instruction__31_26[2], Instruction__31_26[3], ~Instruction__31_26[4], Instruction__31_26[5]);  // AND_Gate
  and beq (out_3, ~Instruction__31_26[0], ~Instruction__31_26[1], Instruction__31_26[2], ~Instruction__31_26[3], ~Instruction__31_26[4], ~Instruction__31_26[5]);  // AND_Gate
  or or_1 (out_8, out_4, out_7);
  or or_2 (out_9, out_6[1], out_4);

  assign out_5 = out_4;
  assign out_6[0] = out_3;
  assign Outputs = out_6[1];

  // Other names for the same wires on the sheet: ALUOp[1:0] = {out_6[1], out_3}; ALUOp0 = out_3; Branch = out_3;
  //   ALUOp1 = out_6[1]; RegDst = out_6[1]; ALUSrc = out_8; Instruction[5:0] = Instruction__31_26; MemRead = out_4;
  //   MemtoReg = out_4; MemWrite = out_7; RegWrite = out_9

  // Notes on the sheet:
  //   RegDst (1): rd signal
  //   Branch (1): branch signal
  //   MemRead (1): read enable signal
  //   ALUOp (2): ALU Control signal
  //   MemWrite (1): Write enable signal
  //   ALUSrc (1): 2nd operand, =0 for rt, =1 for immediate value
  //   RegWrite (1): enable write to one reg
  //   MemtoReg (1): =0 from ALUOutput (R-type), =1 from MDR (lw)
  //   ALUOp
  //   00 Add for L/S
  //   01 Sub for beq
  //   10 from FUNCT field
endmodule
