// Logisim project Data Memory.circ as structural Verilog: 1 circuit, main circuit main
module main (
  input  [7:0] Address,
  input  [31:0] Write_Data,
  input  MemWrite,
  input  MemRead,
  input  CLK,
  output [31:0] Read_Data
);

  RAM #(.dataWidth(32), .bus("separate")) ram_1 (
    .addr(Address), .din(Write_Data), .data(Read_Data), .str(MemWrite), .clk(CLK), .ld(MemRead));  // open: sel, clr
endmodule
