// Logisim project Instruction Memory.circ as structural Verilog: 1 circuit, main circuit main
module main (
  input  [7:0] Read_address,
  output [31:0] Instruction
);

  ROM #(.dataWidth(32)) rom_1 (.addr(Read_address), .data(Instruction));  // open: sel
endmodule
