// Logisim project PC.circ as structural Verilog: 1 circuit, main circuit main
module main (
  input  [31:0] in_1,
  output [7:0] out_2
);

  wire [31:8] register_1_q;

  Register #(.width(32)) register_1 (.D(in_1), .Q({register_1_q, out_2}));  // open: en, clk, clr
endmodule
