// Logisim project ALU Control.circ as structural Verilog: 1 circuit, main circuit main
module main (
  input  [5:0] Instruction__5_0,
  input  [2:0] ALUOp,
  output [2:0] ALUCtl
);

  wire ADD_out, OR_out, SLL_out, SLT_out, SRL_out, SUB_out, XOR_out;
  wire [2:0] _0_out;

  and ADD (ADD_out, ~Instruction__5_0[0], ~Instruction__5_0[1], ~Instruction__5_0[2], ~Instruction__5_0[3], ~Instruction__5_0[4], Instruction__5_0[5]);  // AND_Gate
  // AND_Gate AND has open pins: in0=Instruction__5_0[0], in1=Instruction__5_0[1], in2=Instruction__5_0[2], in3=Instruction__5_0[3], in4=Instruction__5_0[4], in5=Instruction__5_0[5], out=open
  and OR (OR_out, Instruction__5_0[0], ~Instruction__5_0[1], Instruction__5_0[2], ~Instruction__5_0[3], ~Instruction__5_0[4], Instruction__5_0[5]);  // AND_Gate
  and SUB (SUB_out, ~Instruction__5_0[0], Instruction__5_0[1], ~Instruction__5_0[2], ~Instruction__5_0[3], ~Instruction__5_0[4], Instruction__5_0[5]);  // AND_Gate
  and SLT (SLT_out, ~Instruction__5_0[0], Instruction__5_0[1], ~Instruction__5_0[2], Instruction__5_0[3], ~Instruction__5_0[4], Instruction__5_0[5]);  // AND_Gate
  and XOR (XOR_out, ~Instruction__5_0[0], Instruction__5_0[1], Instruction__5_0[2], ~Instruction__5_0[3], ~Instruction__5_0[4], Instruction__5_0[5]);  // AND_Gate
  and SLL (SLL_out, ~Instruction__5_0[0], ~Instruction__5_0[1], ~Instruction__5_0[2], ~Instruction__5_0[3], ~Instruction__5_0[4], ~Instruction__5_0[5]);  // AND_Gate
  and SRL (SRL_out, ~Instruction__5_0[0], Instruction__5_0[1], ~Instruction__5_0[2], ~Instruction__5_0[3], ~Instruction__5_0[4], ~Instruction__5_0[5]);  // AND_Gate
  // AND_Gate JR has open pins: in0=Instruction__5_0[0], in1=Instruction__5_0[1], in2=Instruction__5_0[2], in3=Instruction__5_0[3], in4=Instruction__5_0[4], in5=Instruction__5_0[5], out=open
  or _2 (_0_out[2], SLT_out, SLL_out, SRL_out, XOR_out);
  or _1 (_0_out[1], OR_out, SLL_out, SRL_out, SUB_out);
  or _0 (_0_out[0], ADD_out, SUB_out, XOR_out, SLL_out);
  Multiplexer #(.select(3), .width(3)) multiplexer_1 (
    .in0(3'b001), .in1(3'b011), .in2(_0_out), .in3(3'b010), .in4(3'b000), .in6(3'b110), .in7(3'b111),
    .out(ALUCtl), .sel(ALUOp));  // open: in5, en

  // Other names for the same wires on the sheet: FUNCT[5:0] = Instruction__5_0
endmodule
