// Logisim project Control Unit.circ as structural Verilog: 1 circuit, main circuit main
module main (
  input  [5:0] Instruction__31_26,
  input  [5:0] FUNCT,
  output [4:0] EX,
  output [2:0] MEM,
  output [1:0] WB,
  output Jump,
  output JAL,
  output JR
);

  wire ADDI_out, ANDI_out, J_out, JR_Func_out, JR_out, ORI_out, sll_Func_out, srl_Func_out;

  and R (EX[0], ~Instruction__31_26[0], ~Instruction__31_26[1], ~Instruction__31_26[2], ~Instruction__31_26[3], ~Instruction__31_26[4], ~Instruction__31_26[5]);  // AND_Gate
  and lw (MEM[1], Instruction__31_26[0], Instruction__31_26[1], ~Instruction__31_26[2], ~Instruction__31_26[3], ~Instruction__31_26[4], Instruction__31_26[5]);  // AND_Gate
  and sw (MEM[2], Instruction__31_26[0], Instruction__31_26[1], ~Instruction__31_26[2], Instruction__31_26[3], ~Instruction__31_26[4], Instruction__31_26[5]);  // AND_Gate
  and beq (MEM[0], ~Instruction__31_26[0], ~Instruction__31_26[1], Instruction__31_26[2], ~Instruction__31_26[3], ~Instruction__31_26[4], ~Instruction__31_26[5]);  // AND_Gate
  and ADDI (ADDI_out, ~Instruction__31_26[0], ~Instruction__31_26[1], ~Instruction__31_26[2], Instruction__31_26[3], ~Instruction__31_26[4], ~Instruction__31_26[5]);  // AND_Gate
  and ANDI (ANDI_out, ~Instruction__31_26[0], ~Instruction__31_26[1], Instruction__31_26[2], Instruction__31_26[3], ~Instruction__31_26[4], ~Instruction__31_26[5]);  // AND_Gate
  and ORI (ORI_out, Instruction__31_26[0], ~Instruction__31_26[1], Instruction__31_26[2], Instruction__31_26[3], ~Instruction__31_26[4], ~Instruction__31_26[5]);  // AND_Gate
  and J (J_out, ~Instruction__31_26[0], Instruction__31_26[1], ~Instruction__31_26[2], ~Instruction__31_26[3], ~Instruction__31_26[4], ~Instruction__31_26[5]);  // AND_Gate
  and u_JAL (JAL, Instruction__31_26[0], Instruction__31_26[1], ~Instruction__31_26[2], ~Instruction__31_26[3], ~Instruction__31_26[4], ~Instruction__31_26[5]);  // AND_Gate
  and u_JR (JR_out, ~Instruction__31_26[0], ~Instruction__31_26[1], ~Instruction__31_26[2], ~Instruction__31_26[3], ~Instruction__31_26[4], ~Instruction__31_26[5]);  // AND_Gate
  and JR_Func (JR_Func_out, ~FUNCT[0], ~FUNCT[1], ~FUNCT[2], FUNCT[3], ~FUNCT[4], ~FUNCT[5]);  // AND_Gate
  and sll_Func (sll_Func_out, ~FUNCT[0], ~FUNCT[1], ~FUNCT[2], ~FUNCT[3], ~FUNCT[4], ~FUNCT[5]);  // AND_Gate
  and srl_Func (srl_Func_out, ~FUNCT[0], FUNCT[1], ~FUNCT[2], ~FUNCT[3], ~FUNCT[4], ~FUNCT[5]);  // AND_Gate
  or or_1 (EX[4], MEM[1], MEM[2], ADDI_out, ANDI_out, ORI_out);
  or or_2 (WB[0], EX[0], MEM[1], ADDI_out, ANDI_out, ORI_out, JAL);
  or or_3 (EX[3], ANDI_out, sll_Func_out);
  or or_4 (EX[2], EX[0], srl_Func_out, ORI_out);
  or or_5 (EX[1], sll_Func_out, MEM[0], ORI_out, srl_Func_out);
  or or_6 (Jump, J_out, JAL);
  and and_1 (JR, JR_out, JR_Func_out);

  assign WB[1] = MEM[1];

  // Other names for the same wires on the sheet: RegDst = EX[0]; ALUOp[2:0] = EX[3:1]; ALUOp0 = EX[1]; ALUOp1 = EX[2];
  //   ALUOp2 = EX[3]; ALUSrc = EX[4]; Instruction[5:0] = Instruction__31_26; Branch = MEM[0]; MemWrite = MEM[2];
  //   RegWrite = WB[0]; MemRead = MEM[1]; MemtoReg = MEM[1]

  // Notes on the sheet:
  //   011 Or
  //   100 And
  //   110 SRL
  //   111 SLL
  //   ALUOp
  //   000 Add for L/S
  //   001 Sub for beq
  //   010 from FUNCT field
  //   Outputs:
  //   RegDst (1): rd signal
  //   Branch (1): branch signal
  //   MemRead (1): read enable signal
  //   ALUOp (2): ALU Control signal
  //   MemWrite (1): Write enable signal
  //   RegWrite (1): enable write to one reg
  //   Jump (1): high on J
  //   JAL (1): high on JAL
  //   JR (1): high on JR
  //   MemtoReg (1): =0 from ALUOutput (R-type), =1 from MDR (lw)
  //   ALUSrc (1): 2nd operand, =0 for rt, =1 for immediate value
endmodule
