// Logisim project EX.circ as structural Verilog: 1 circuit, main circuit main
module main (
  input  [4:0] in_1,
  input  in_2,
  output out_3,
  output [4:0] out_4
);

  Register #(.width(5)) register_1 (.D(in_1), .Q(out_4), .clk(in_2));  // open: en, clr

  assign out_3 = in_2;

  // Other names for the same wires on the sheet: CLK = in_2; In[4:0] = in_1; Out[4:0] = out_4
endmodule
