// Logisim project EX_MEM.circ as structural Verilog: 1 circuit, main circuit main
module main (
  input  [31:0] in_1,
  input  in_2,
  input  [31:0] in_3,
  input  [31:0] in_4,
  input  [4:0] in_5,
  input  CLK,
  output out_7,
  output [31:0] out_8,
  output out_9,
  output [31:0] out_10,
  output [31:0] out_11,
  output [4:0] out_12
);

  Register #(.width(32)) register_1 (.D(in_1), .Q(out_8), .clk(CLK));  // open: en, clr
  Register #(.width(1)) register_2 (.D(in_2), .Q(out_9), .clk(CLK));  // open: en, clr
  Register #(.width(32)) register_3 (.D(in_3), .Q(out_10), .clk(CLK));  // open: en, clr
  Register #(.width(32)) register_4 (.D(in_4), .Q(out_11), .clk(CLK));  // open: en, clr
  Register #(.width(5)) register_5 (.D(in_5), .Q(out_12), .clk(CLK));  // open: en, clr

  assign out_7 = CLK;

  // Other names for the same wires on the sheet: ALUResult[31:0] = in_3; ALUResult_Out[31:0] = out_10;
  //   Branch_Addr[31:0] = in_1; Branch_Addr_Out[31:0] = out_8; RegDst[4:0] = in_5; RegDst_Out[4:0] = out_12;
  //   SW_Data[31:0] = in_4; SW_Data_Out[31:0] = out_11; Zero = in_2; Zero_Out = out_9
endmodule
