// Logisim project Forwarding Unit.circ as structural Verilog: 1 circuit, main circuit main
module main (
  input  [4:0] EX_MEM_RegRd,
  input  EX_MEM_RegWrite,
  input  [4:0] ID_EX_Rs,
  input  [4:0] MEM_WB_RegRd,
  input  [4:0] ID_EX_Rt,
  input  MEM_WB_RegWrite,
  output [1:0] ForwardA,
  output [1:0] ForwardB
);

  wire comparator_1_eq, comparator_2_eq, comparator_3_eq, comparator_4_eq, comparator_5_eq, comparator_6_eq,
       comparator_7_eq, comparator_8_eq, comparator_9_eq, comparator_10_eq, Ex_A_Control, Ex_B_Control,
       MEM_A_Control, MEM_B_Control, not_1_out, not_2_out, not_3_out, not_4_out, not_5_out, not_6_out;
  wire [1:0] ForwardA_Ex, ForwardA_MEM, ForwardB_Ex, ForwardB_MEM, multiplexer_5_out, multiplexer_6_out;

  not not_1 (not_1_out, comparator_1_eq);
  Comparator #(.width(5)) comparator_1 (.a(EX_MEM_RegRd), .b({5{1'b0}}), .eq(comparator_1_eq));  // open: gt, lt
  Comparator #(.width(5)) comparator_2 (.a(EX_MEM_RegRd), .b(ID_EX_Rs), .eq(comparator_2_eq));  // open: gt, lt
  not not_2 (not_2_out, comparator_3_eq);
  Comparator #(.width(5)) comparator_3 (.a(EX_MEM_RegRd), .b({5{1'b0}}), .eq(comparator_3_eq));  // open: gt, lt
  Comparator #(.width(5)) comparator_4 (.a(EX_MEM_RegRd), .b(ID_EX_Rt), .eq(comparator_4_eq));  // open: gt, lt
  not not_3 (not_3_out, comparator_5_eq);
  Comparator #(.width(5)) comparator_5 (.a(MEM_WB_RegRd), .b({5{1'b0}}), .eq(comparator_5_eq));  // open: gt, lt
  Comparator #(.width(2)) comparator_6 (.a(ForwardA_Ex), .b(2'b10), .eq(comparator_6_eq));  // open: gt, lt
  not not_4 (not_4_out, comparator_6_eq);
  Comparator #(.width(5)) comparator_7 (.a(MEM_WB_RegRd), .b(ID_EX_Rs), .eq(comparator_7_eq));  // open: gt, lt
  not not_5 (not_5_out, comparator_8_eq);
  Comparator #(.width(5)) comparator_8 (.a(MEM_WB_RegRd), .b({5{1'b0}}), .eq(comparator_8_eq));  // open: gt, lt
  not not_6 (not_6_out, comparator_9_eq);
  Comparator #(.width(2)) comparator_9 (.a(ForwardB_Ex), .b(2'b10), .eq(comparator_9_eq));  // open: gt, lt
  Comparator #(.width(5)) comparator_10 (.a(MEM_WB_RegRd), .b(ID_EX_Rt), .eq(comparator_10_eq));  // open: gt, lt
  and and_1 (Ex_A_Control, EX_MEM_RegWrite, not_1_out, comparator_2_eq);
  and and_2 (Ex_B_Control, EX_MEM_RegWrite, not_2_out, comparator_4_eq);
  and and_3 (MEM_A_Control, MEM_WB_RegWrite, not_3_out, not_4_out, comparator_7_eq);
  and and_4 (MEM_B_Control, MEM_WB_RegWrite, not_5_out, not_6_out, comparator_10_eq);
  Multiplexer #(.width(2)) multiplexer_1 (.in0(2'b00), .in1(2'b10), .out(ForwardA_Ex), .sel(Ex_A_Control));  // open: en
  Multiplexer #(.width(2)) multiplexer_2 (.in0(2'b00), .in1(2'b10), .out(ForwardB_Ex), .sel(Ex_B_Control));  // open: en
  Multiplexer #(.width(2)) multiplexer_3 (
    .in0(2'b00), .in1(2'b01), .out(ForwardA_MEM), .sel(MEM_A_Control));  // open: en
  Multiplexer #(.width(2)) multiplexer_4 (
    .in0(2'b00), .in1(2'b01), .out(ForwardB_MEM), .sel(MEM_B_Control));  // open: en
  Multiplexer #(.select(2), .width(2)) multiplexer_5 (
    .in0(2'b00), .in1(2'b01), .out(multiplexer_5_out), .sel(ForwardA_MEM));  // open: in2, in3, en
  Multiplexer #(.select(2), .width(2)) multiplexer_6 (
    .in0(2'b00), .in1(2'b01), .out(multiplexer_6_out), .sel(ForwardB_MEM));  // open: in2, in3, en
  Multiplexer #(.select(2), .width(2)) multiplexer_7 (
    .in0(multiplexer_5_out), .in2(2'b10), .out(ForwardA), .sel(ForwardA_Ex));  // open: in1, in3, en
  Multiplexer #(.select(2), .width(2)) multiplexer_8 (
    .in0(multiplexer_6_out), .in2(2'b10), .out(ForwardB), .sel(ForwardB_Ex));  // open: in1, in3, en
  // Probe on ForwardA_MEM
  // Probe on ForwardB_MEM
  // Probe on ForwardA_Ex
  // Probe on ForwardB_Ex
endmodule
