// Logisim project Forwarding Unit_ID.circ as structural Verilog: 1 circuit, main circuit main
module main (
  input  ID_Branch,
  input  [4:0] EX_MEM_RegRd,
  input  [4:0] IF_ID_RegRs,
  input  [4:0] IF_ID_RegRt,
  output ForwardC,
  output ForwardD
);

  wire comparator_1_eq, comparator_2_eq, comparator_3_eq, comparator_4_eq, not_1_out, not_2_out;

  not not_1 (not_1_out, comparator_1_eq);
  Comparator #(.width(5)) comparator_1 (.a(EX_MEM_RegRd), .b({5{1'b0}}), .eq(comparator_1_eq));  // open: gt, lt
  Comparator #(.width(5)) comparator_2 (.a(EX_MEM_RegRd), .b(IF_ID_RegRs), .eq(comparator_2_eq));  // open: gt, lt
  Comparator #(.width(5)) comparator_3 (.a(EX_MEM_RegRd), .b({5{1'b0}}), .eq(comparator_3_eq));  // open: gt, lt
  not not_2 (not_2_out, comparator_3_eq);
  Comparator #(.width(5)) comparator_4 (.a(EX_MEM_RegRd), .b(IF_ID_RegRt), .eq(comparator_4_eq));  // open: gt, lt
  and and_1 (ForwardC, ID_Branch, not_1_out, comparator_2_eq);
  and and_2 (ForwardD, ID_Branch, not_2_out, comparator_4_eq);
endmodule
