// Logisim project Hazard Detection.circ as structural Verilog: 1 circuit, main circuit main
module main (
  input  ID_EX_MemRead,
  input  [4:0] IF_ID_RegRs,
  input  [4:0] IF_ID_RegRt,
  input  [4:0] ID_EX_RegRt,
  output PCWrite,
  output IF_ID_Write,
  output CU_Control
);

  wire comparator_1_eq, comparator_2_eq, or_1_out, Stall;

  Comparator #(.width(5)) comparator_1 (.a(ID_EX_RegRt), .b(IF_ID_RegRs), .eq(comparator_1_eq));  // open: gt, lt
  Comparator #(.width(5)) comparator_2 (.a(ID_EX_RegRt), .b(IF_ID_RegRt), .eq(comparator_2_eq));  // open: gt, lt
  or or_1 (or_1_out, comparator_1_eq, comparator_2_eq);
  and and_1 (Stall, ID_EX_MemRead, or_1_out);
  Multiplexer multiplexer_1 (.in0(1'b1), .in1(1'b0), .out(IF_ID_Write), .sel(Stall));  // open: en
  Multiplexer multiplexer_2 (.in0(1'b1), .in1(1'b0), .out(PCWrite), .sel(Stall));  // open: en
  Multiplexer multiplexer_3 (.in0(1'b0), .in1(1'b1), .out(CU_Control), .sel(Stall));  // open: en

  // Notes on the sheet:
  //   Stall = 0
  //   Stall = 1
  //   Writes = 1
  //   Writes = 0
  //   Control = 0
  //   Control = 1
endmodule
