// Logisim project ID_EX.circ as structural Verilog: 1 circuit, main circuit main
module main (
  input  [31:0] in_1,
  input  [31:0] in_2,
  input  [31:0] in_3,
  input  [31:0] in_4,
  input  [4:0] in_5,
  input  [4:0] in_6,
  input  [4:0] in_7,
  input  [4:0] in_8,
  input  [4:0] in_9,
  input  CLK,
  output out_11,
  output [31:0] out_12,
  output [31:0] out_13,
  output [31:0] out_14,
  output [31:0] out_15,
  output [4:0] out_16,
  output [4:0] out_17,
  output [4:0] out_18,
  output [4:0] out_19,
  output [4:0] out_20
);

  Register #(.width(32)) register_1 (.D(in_1), .Q(out_12), .clk(CLK));  // open: en, clr
  Register #(.width(32)) register_2 (.D(in_2), .Q(out_13), .clk(CLK));  // open: en, clr
  Register #(.width(32)) register_3 (.D(in_3), .Q(out_14), .clk(CLK));  // open: en, clr
  Register #(.width(32)) register_4 (.D(in_4), .Q(out_15), .clk(CLK));  // open: en, clr
  Register #(.width(5)) register_5 (.D(in_5), .Q(out_16), .clk(CLK));  // open: en, clr
  Register #(.width(5)) register_6 (.D(in_6), .Q(out_17), .clk(CLK));  // open: en, clr
  Register #(.width(5)) register_7 (.D(in_7), .Q(out_18), .clk(CLK));  // open: en, clr
  Register #(.width(5)) register_8 (.D(in_8), .Q(out_19), .clk(CLK));  // open: en, clr
  Register #(.width(5)) register_9 (.D(in_5), .Q(out_16), .clk(CLK));  // open: en, clr

  assign in_9 = in_5;
  assign out_11 = CLK;
  assign out_20 = out_16;

  // Other names for the same wires on the sheet: Inst_10_6[4:0] = in_7; Inst_10_6__Out[4:0] = out_18;
  //   Inst_15_0[31:0] = in_4; Inst_15_0__Out[31:0] = out_15; Inst_15_11[4:0] = in_6; Inst_15_11__Out[4:0] = out_17;
  //   Inst_20_16[4:0] = in_5; Inst_20_16__Out[4:0] = out_16; Inst_25_21[4:0] = in_8; Inst_25_21__Out[4:0] = out_19;
  //   PC_4[31:0] = in_1; PC_4_Out[31:0] = out_12; Read1[31:0] = in_2; Read1_Out[31:0] = out_13; Read2[31:0] = in_3;
  //   Read2_Out[31:0] = out_14
endmodule
