// Logisim project IF_ID.circ as structural Verilog: 1 circuit, main circuit main
module main (
  input  in_1,
  input  [31:0] PC_4,
  input  [31:0] Instruction,
  input  [31:0] PC,
  input  CLK,
  output [31:0] PC_4_2,
  output [31:0] Instruction_2,
  output [31:0] PC_Out
);

  Register #(.width(32)) register_1 (.D(PC_4), .en(in_1), .Q(PC_4_2), .clk(CLK));  // open: clr
  Register #(.width(32)) register_2 (.D(Instruction), .en(in_1), .Q(Instruction_2), .clk(CLK));  // open: clr
  Register #(.width(32)) register_3 (.D(PC), .en(in_1), .Q(PC_Out), .clk(CLK));  // open: clr

  // Other names for the same wires on the sheet: Enable = in_1; Instruction_Out[31:0] = Instruction_2;
  //   PC_4_Out[31:0] = PC_4_2
endmodule
