// Logisim project Instruction Memory Basic.circ as structural Verilog: 1 circuit, main circuit main
module main (
  input  [7:0] Read_address,
  output [31:0] Instruction
);

  ROM #(.dataWidth(32)) rom_1 (.addr(Read_address), .data(Instruction));  // open: sel

  // Notes on the sheet:
  //   contents of rom_1 (hex, n*v repeats v):
  //   20010001 20020002 34030003 34040004 20050005 20060006 20070007 ac01000c 224020 8c6f0009 224824
  //   825022 a35825 e66026 a6682a c5702a 30300001 18a80 79082
endmodule
