// Logisim project Instruction Memory Final.circ as structural Verilog: 1 circuit, main circuit main
module main (
  input  [7:0] Read_address,
  output [31:0] Instruction
);

  ROM #(.dataWidth(32)) rom_1 (.addr(Read_address), .data(Instruction));  // open: sel

  // Notes on the sheet:
  //   contents of rom_1 (hex, n*v repeats v):
  //   34010001 211020 221826 2064000e 232824 aca4000b 8ca6000b c43824 10e10003 c7402a 11080001 201cffff
  //   20090001 8c0a000c ad4a0013 8c0a000c 1141fffb c000013 201bffff 23ff0018 ac1f0000 8c0b0000 1600008
  //   201affff 8000018 2019ffff 2018ffff
endmodule
