// Logisim project Instruction Memory Forwarding.circ as structural Verilog: 1 circuit, main circuit main
module main (
  input  [7:0] Read_address,
  output [31:0] Instruction
);

  ROM #(.dataWidth(32)) rom_1 (.addr(Read_address), .data(Instruction));  // open: sel

  // Notes on the sheet:
  //   contents of rom_1 (hex, n*v repeats v):
  //   20010001 5*210820 ac010000 8c020000 211824 ac630000 8c640000 ac640004
endmodule
