// Logisim project Instruction Memory.circ as structural Verilog: 1 circuit, main circuit main
module main (
  input  [7:0] Read_address,
  output [31:0] Instruction
);

  ROM #(.dataWidth(32)) rom_1 (.addr(Read_address), .data(Instruction));  // open: sel

  // Notes on the sheet:
  //   contents of rom_1 (hex, n*v repeats v):
  //   20010008 34220005 3043ffff 612020 832822 223024 c33826 aca40064 8ca80064 22482a 1265025 c00000d
  //   200b0001 23ff0018 10c00003 a13022 800000e 200c0001 3e00008 200d0001 200e0001
endmodule
