// Logisim project Lab 3 Given.circ as structural Verilog: 4 circuits, main circuit Main
module Main (
);

  wire ALUSrc, CLK, comparator_1_eq, CU_Control, EX_MEM_RegWrite, ForwardC, ForwardD, ID_Branch,
       ID_EX_MemRead, IF_Flush, IF_ID_Write, JAL, JR, JUMP, main_12_out_3, main_13_out_3, main_14_p9,
       main_18_out_3, main_19_out_7, main_22_out_6, MEM_WB_JAL, MEM_WB_JR, MEM_WB_RegWrite, MemRead,
       MemtoReg, MemWrite, PCSrc, PCWrite, RegDst;
  wire [0:0] main_18_out_4;
  wire [1:0] ForwardA, ForwardB;
  wire [2:0] ALUCtrl, ALUOp, main_12_out_4, multiplexer_8_out;
  wire [2:1] MEM;
  wire [3:0] main_11_out_4, multiplexer_7_out, WB;
  wire [3:1] main_17_out_4;
  wire [4:0] EX, EX_MEM_RegRd, ID_EX_Rs, ID_EX_Rt, IF_ID_Rs, IF_ID_Rt, Inst_10_6, main_14_p15, main_14_p16,
       main_22_out_10, MEM_WB_RegRd, multiplexer_9_out, multiplexer_13_out, Shamt;
  wire [5:0] Inst_5_0, Inst_31_26;
  wire [7:0] PC;
  wire [15:11] Inst_15_0;
  wire [31:0] ALU_A, ALU_B, ALUResult, Branch_Addr, EX_MEM_data, IF_ID_PC, Instruction, JRAddr, main_1_out_4,
       main_3_instruction, main_6_pc_4_2, main_8_out_2, main_10_p2, main_14_p11, main_14_p12, main_14_p13,
       main_14_p14, main_19_out_8, main_20_read_data, main_22_out_7, main_22_out_8, main_22_out_9,
       MEM_WB_data, MemData, multiplexer_1_out, multiplexer_2_out, multiplexer_3_out, multiplexer_5_out,
       multiplexer_6_out, multiplexer_11_out, PC_4, register_file_1_rddata1, register_file_1_rddata2;

  Multiplexer #(.width(32)) multiplexer_1 (
    .in0(PC_4), .in1(Branch_Addr), .out(multiplexer_1_out), .sel(PCSrc));  // open: en
  Multiplexer #(.width(32)) multiplexer_2 (
    .in0(multiplexer_1_out),
    .in1({IF_ID_PC[31:28], IF_ID_Rs, IF_ID_Rt, Inst_15_0, Inst_10_6, Inst_5_0, 2'b00}),
    .out(multiplexer_2_out), .sel(JUMP));  // open: en
  Multiplexer #(.width(32)) multiplexer_3 (
    .in0(multiplexer_2_out), .in1(JRAddr), .out(multiplexer_3_out), .sel(MEM_WB_JR));  // open: en
  PC_main main_1 (
    .in_2(multiplexer_3_out), .out_4({main_1_out_4[31:10], PC, main_1_out_4[1:0]}), .in_3(CLK), .in_1(PCWrite));
  Adder #(.width(32)) adder_1 (
    .a({main_1_out_4[31:10], PC, main_1_out_4[1:0]}), .b(32'h4), .out(PC_4));  // open: cin, cout
  // Instruction_Memory_Forwarding_main main_2: pin names not known
  Instruction_Memory_Final_main main_3 (.Read_address(PC), .Instruction(main_3_instruction));
  // Instruction_Memory_Basic_main main_4: pin names not known
  Multiplexer #(.width(32)) multiplexer_4 (
    .in0(main_3_instruction), .in1({32{1'b0}}), .out(Instruction), .sel(IF_Flush));  // open: en
  Hazard_Detection_main main_5 (
    .ID_EX_RegRt(ID_EX_Rt), .IF_ID_RegRs(IF_ID_Rs), .IF_ID_RegRt(IF_ID_Rt), .ID_EX_MemRead(ID_EX_MemRead),
    .IF_ID_Write(IF_ID_Write), .PCWrite(PCWrite), .CU_Control(CU_Control));
  IF_ID_main main_6 (
    .PC_4(PC_4), .Instruction(Instruction), .PC_4_2(main_6_pc_4_2),
    .Instruction_2({Inst_31_26, IF_ID_Rs, IF_ID_Rt, Inst_15_0, Inst_10_6, Inst_5_0}), .CLK(CLK),
    .in_1(IF_ID_Write), .PC({main_1_out_4[31:10], PC, main_1_out_4[1:0]}), .PC_Out(IF_ID_PC));
  Register_File register_file_1 (
    .WrAddr(MEM_WB_RegRd), .WrData(MEM_WB_data), .WrReg(MEM_WB_RegWrite), .RdAddr1(IF_ID_Rs),
    .RdAddr2(IF_ID_Rt), .RdData1(register_file_1_rddata1), .RdData2(register_file_1_rddata2), .Clock(CLK));
  Control_Unit_main main_7 (
    .Instruction__31_26(Inst_31_26), .FUNCT(Inst_5_0), .EX(EX), .MEM({MEM, ID_Branch}), .WB(WB),
    .PCSrc(PCSrc), .Jump(JUMP), .JAL(JAL), .JR(JR), .IF_Flush(IF_Flush));
  Sign_extension_main main_8 (.in_1({Inst_15_0, Inst_10_6, Inst_5_0}), .out_2(main_8_out_2));
  Forwarding_Unit_ID_main main_9 (
    .ID_Branch(ID_Branch), .EX_MEM_RegRd(EX_MEM_RegRd), .IF_ID_RegRs(IF_ID_Rs), .IF_ID_RegRt(IF_ID_Rt),
    .ForwardC(ForwardC), .ForwardD(ForwardD));
  Multiplexer #(.width(32)) multiplexer_5 (
    .in0(register_file_1_rddata1), .in1(EX_MEM_data), .out(multiplexer_5_out), .sel(ForwardC));  // open: en
  Multiplexer #(.width(32)) multiplexer_6 (
    .in0(register_file_1_rddata2), .in1(EX_MEM_data), .out(multiplexer_6_out), .sel(ForwardD));  // open: en
  // Left_shift_2_main main_10: pin names not known; wires that end beside it: main_8_out_2, main_10_p2
  Multiplexer #(.width(4)) multiplexer_7 (
    .in0(WB), .in1(4'b0000), .out(multiplexer_7_out), .sel(CU_Control));  // open: en
  WB_main main_11 (.in_1(multiplexer_7_out), .out_4(main_11_out_4), .in_2(main_12_out_3));  // open: out_3
  Multiplexer #(.width(3)) multiplexer_8 (
    .in0({MEM, ID_Branch}), .in1(3'b000), .out(multiplexer_8_out), .sel(CU_Control));  // open: en
  MEM_main main_12 (
    .in_1(multiplexer_8_out), .out_4({main_12_out_4[2], ID_EX_MemRead, main_12_out_4[0]}),
    .out_3(main_12_out_3), .in_2(main_13_out_3));
  Multiplexer #(.width(5)) multiplexer_9 (
    .in0(EX), .in1({5{1'b0}}), .out(multiplexer_9_out), .sel(CU_Control));  // open: en
  and and_1 (PCSrc, ID_Branch, comparator_1_eq);
  Comparator #(.width(32)) comparator_1 (
    .a(multiplexer_5_out), .b(multiplexer_6_out), .eq(comparator_1_eq));  // open: gt, lt
  Adder #(.width(32)) adder_2 (.a(main_6_pc_4_2), .b(main_10_p2), .out(Branch_Addr));  // open: cin, cout
  EX_main main_13 (.in_1(multiplexer_9_out), .out_4({ALUSrc, ALUOp, RegDst}), .out_3(main_13_out_3), .in_2(main_14_p9));
  // ID_EX_main main_14: pin names not known; wires that end beside it: main_6_pc_4_2, multiplexer_5_out, multiplexer_6_out, main_8_out_2, IF_ID_Rt, Inst_15_0, Inst_10_6, IF_ID_Rs, main_14_p9, CLK, main_14_p11, main_14_p12, main_14_p13, main_14_p14, main_14_p15, main_14_p16, Shamt, ID_EX_Rs
  // Probe on ID_EX_Rs
  // Probe on ID_EX_Rt
  Multiplexer #(.width(32)) multiplexer_10 (
    .in0(multiplexer_11_out), .in1(main_14_p14), .out(ALU_B), .sel(ALUSrc));  // open: en
  Multiplexer #(.select(2), .width(32)) multiplexer_11 (
    .in0(main_14_p13), .in1(MEM_WB_data), .in2(EX_MEM_data), .out(multiplexer_11_out), .sel(ForwardB));  // open: in3, en
  Forwarding_Unit_main main_15 (
    .ForwardA(ForwardA), .ForwardB(ForwardB), .ID_EX_Rs(ID_EX_Rs), .ID_EX_Rt(ID_EX_Rt),
    .EX_MEM_RegRd(EX_MEM_RegRd), .EX_MEM_RegWrite(EX_MEM_RegWrite), .MEM_WB_RegRd(MEM_WB_RegRd),
    .MEM_WB_RegWrite(MEM_WB_RegWrite));
  ALU alu_1 (.ALUCtl(ALUCtrl), .A(ALU_A), .B(ALU_B), .ALUResult(ALUResult), .Shamt(Shamt));  // open: Zero, Overflow
  Multiplexer #(.select(2), .width(32)) multiplexer_12 (
    .in0(main_14_p12), .in1(MEM_WB_data), .in2(EX_MEM_data), .out(ALU_A), .sel(ForwardA));  // open: in3, en
  ALU_Control_main main_16 (.Instruction__5_0(main_14_p14[5:0]), .ALUCtl(ALUCtrl), .ALUOp(ALUOp));
  Multiplexer #(.width(5)) multiplexer_13 (
    .in0(main_14_p15), .in1(main_14_p16), .out(multiplexer_13_out), .sel(RegDst));  // open: en
  WB_main main_17 (
    .in_1(main_11_out_4), .out_4({main_17_out_4, EX_MEM_RegWrite}), .in_2(main_18_out_3));  // open: out_3
  MEM_main main_18 (
    .in_1({main_12_out_4[2], ID_EX_MemRead, main_12_out_4[0]}),
    .out_4({MemWrite, MemRead, main_18_out_4[0]}), .out_3(main_18_out_3), .in_2(main_19_out_7));
  EX_MEM_main main_19 (
    .in_1(main_14_p11), .in_3(ALUResult), .in_4(multiplexer_11_out), .in_5(multiplexer_13_out),
    .out_8(main_19_out_8), .out_10(EX_MEM_data), .out_11(MemData), .out_12(EX_MEM_RegRd),
    .out_7(main_19_out_7), .CLK(CLK));  // open: in_2, out_9
  Data_Memory_main main_20 (
    .Address(EX_MEM_data[9:2]), .Write_Data(MemData), .Read_Data(main_20_read_data), .MemWrite(MemWrite),
    .CLK(CLK), .MemRead(MemRead));
  WB_main main_21 (
    .in_1({main_17_out_4, EX_MEM_RegWrite}), .out_4({MEM_WB_JR, MEM_WB_JAL, MemtoReg, MEM_WB_RegWrite}),
    .in_2(main_22_out_6));  // open: out_3
  MEM_WB_main main_22 (
    .in_2(main_20_read_data), .in_3(EX_MEM_data), .in_4(EX_MEM_RegRd), .out_8(main_22_out_8),
    .out_9(main_22_out_9), .out_10(main_22_out_10), .out_6(main_22_out_6), .CLK(CLK), .in_1(main_19_out_8),
    .out_7(main_22_out_7));
  Multiplexer #(.width(32)) multiplexer_14 (
    .in0(main_22_out_9), .in1(main_22_out_8), .out(JRAddr), .sel(MemtoReg));  // open: en
  Multiplexer #(.width(5)) multiplexer_15 (
    .in0(main_22_out_10), .in1({5{1'b1}}), .out(MEM_WB_RegRd), .sel(MEM_WB_JAL));  // open: en
  Multiplexer #(.width(32)) multiplexer_16 (
    .in0(JRAddr), .in1(main_22_out_7), .out(MEM_WB_data), .sel(MEM_WB_JAL));  // open: en
  // Probe on Instruction
  // Probe on ALUResult
  // Probe on PC
  // Probe on ID_Branch
  // Probe on JUMP
  // Probe on JAL
  // Probe on JR
  // Probe on MEM_WB_RegWrite
  // Probe on MEM_WB_RegRd
  // Probe on MEM_WB_data
  // Probe on MemWrite
  // Probe on MemData
  Clock u_CLK (.out(CLK));
  // Probe on ForwardA
  // Probe on ForwardB
  // Probe on ForwardC
  // Probe on ForwardD
  // Probe on ALU_A
  // Probe on ALU_B

  // Other names for the same wires on the sheet: Inst_15_0[10:0] = {Inst_10_6, Inst_5_0};
  //   JumpAddr[31:2] = {IF_ID_PC[31:28], IF_ID_Rs, IF_ID_Rt, Inst_15_0, Inst_10_6, Inst_5_0};
  //   Inst_15_11[4:0] = Inst_15_0; Inst_20_16[4:0] = IF_ID_Rt; Inst_25_21[4:0] = IF_ID_Rs; MEM[0] = ID_Branch;
  //   WrAddr[4:0] = MEM_WB_RegRd; WrData[31:0] = MEM_WB_data
endmodule

module ALU (
  input  [2:0] ALUCtl,
  input  [31:0] A,
  input  [31:0] B,
  input  [4:0] Shamt,
  output [31:0] ALUResult,
  output Zero,
  output Overflow
);

  wire comparator_1_lt, comparator_2_lt, comparator_3_eq, comparator_4_eq, or_2_out;
  wire [31:0] ADD, AND, NOR, OR, SLL, SLT, SLTU, SRL, SUB, XOR;

  assign XOR = A ^ B;  // XOR_Gate xor_1, 32 bits wide
  Adder #(.width(32)) adder_1 (.a(A), .b(B), .out(ADD));  // open: cin, cout
  Subtractor #(.width(32)) subtractor_1 (.a(A), .b(B), .out(SUB));  // open: bin, bout
  assign AND = A & B;  // AND_Gate and_1, 32 bits wide
  assign OR = A | B;  // OR_Gate or_1, 32 bits wide
  assign NOR = ~(A | B);  // NOR_Gate nor_1, 32 bits wide
  Comparator #(.width(32)) comparator_1 (.a(A), .b(B), .lt(comparator_1_lt));  // open: gt, eq
  assign SLT = {{31{1'b0}}, comparator_1_lt};  // Bit_Extender bit_extender_1
  Shifter #(.width(32)) shifter_1 (.in(B), .\dist (Shamt), .out(SLL));
  Shifter #(.width(32), .shift("lr")) shifter_2 (.in(B), .\dist (Shamt), .out(SRL));
  Comparator #(.width(32), .mode("unsigned")) comparator_2 (.a(A), .b(B), .lt(comparator_2_lt));  // open: gt, eq
  assign SLTU = {{31{1'b0}}, comparator_2_lt};  // Bit_Extender bit_extender_2
  Multiplexer #(.select(3), .width(32), .enable("false")) multiplexer_1 (
    .in0(AND), .in1(ADD), .in2(OR), .in3(SUB), .in4(SLT), .in5(XOR), .in6(SRL), .in7(SLL), .out(ALUResult),
    .sel(ALUCtl));
  Comparator #(.width(3)) comparator_3 (.a(3'b001), .b(ALUCtl), .eq(comparator_3_eq));  // open: gt, lt
  Comparator #(.width(3)) comparator_4 (.a(ALUCtl), .b(3'b011), .eq(comparator_4_eq));  // open: gt, lt
  Overflow_Unit overflow_unit_1 (
    .Add(comparator_3_eq), .Sub(comparator_4_eq), .ASign(A[31]), .BSign(B[31]), .ResultSign(ALUResult[31]),
    .Overflow(Overflow));
  or or_2 (or_2_out, ALUResult[0], ALUResult[1], ALUResult[2], ALUResult[3], ALUResult[4], ALUResult[5], ALUResult[6], ALUResult[7], ALUResult[8], ALUResult[9], ALUResult[10], ALUResult[11], ALUResult[12], ALUResult[13], ALUResult[14], ALUResult[15], ALUResult[16], ALUResult[17], ALUResult[18], ALUResult[19], ALUResult[20], ALUResult[21], ALUResult[22], ALUResult[23], ALUResult[24], ALUResult[25], ALUResult[26], ALUResult[27], ALUResult[28], ALUResult[29], ALUResult[30], ALUResult[31]);
  not not_1 (Zero, or_2_out);

  // Other names for the same wires on the sheet: ASign = A[31]; ResultSign = ALUResult[31]; BSign = B[31]

  // Notes on the sheet:
  //   ALUCtl for ADD on top port
  //   ALUCtl for SUB on second port
endmodule

module Register_File (
  input  [4:0] WrAddr,
  input  [31:0] WrData,
  input  WrReg,
  input  [4:0] RdAddr1,
  input  [4:0] RdAddr2,
  input  Clock,
  output [31:0] RdData1,
  output [31:0] RdData2
);

  wire and_1_out, and_2_out, comparator_1_eq, comparator_2_eq, comparator_3_eq, comparator_4_eq, not_1_out,
       not_2_out, WrReg0, WrReg1, WrReg2, WrReg3, WrReg4, WrReg5, WrReg6, WrReg7, WrReg8, WrReg9, WrReg10,
       WrReg11, WrReg12, WrReg13, WrReg14, WrReg15, WrReg16, WrReg17, WrReg18, WrReg19, WrReg20, WrReg21,
       WrReg22, WrReg23, WrReg24, WrReg25, WrReg26, WrReg27, WrReg28, WrReg29, WrReg30, WrReg31;
  wire [31:0] multiplexer_1_out, multiplexer_2_out, RegData1, RegData2, RegData3, RegData4, RegData5,
       RegData6, RegData7, RegData8, RegData9, RegData10, RegData11, RegData12, RegData13, RegData14,
       RegData15, RegData16, RegData17, RegData18, RegData19, RegData20, RegData21, RegData22, RegData23,
       RegData24, RegData25, RegData26, RegData27, RegData28, RegData29, RegData30, RegData31;

  Demultiplexer #(.select(5), .enable("false")) demultiplexer_1 (
    .out0(WrReg0), .out1(WrReg1), .out2(WrReg2), .out3(WrReg3), .out4(WrReg4), .out5(WrReg5), .out6(WrReg6),
    .out7(WrReg7), .out8(WrReg8), .out9(WrReg9), .out10(WrReg10), .out11(WrReg11), .out12(WrReg12),
    .out13(WrReg13), .out14(WrReg14), .out15(WrReg15), .out16(WrReg16), .out17(WrReg17), .out18(WrReg18),
    .out19(WrReg19), .out20(WrReg20), .out21(WrReg21), .out22(WrReg22), .out23(WrReg23), .out24(WrReg24),
    .out25(WrReg25), .out26(WrReg26), .out27(WrReg27), .out28(WrReg28), .out29(WrReg29), .out30(WrReg30),
    .out31(WrReg31), .in(WrReg), .sel(WrAddr));
  // Probe on RegData4
  Register #(.width(32)) Reg4 (.D(WrData), .en(WrReg4), .Q(RegData4), .clk(Clock));  // open: clr
  // Probe on RegData8
  Register #(.width(32)) Reg8 (.D(WrData), .en(WrReg8), .Q(RegData8), .clk(Clock));  // open: clr
  // Probe on RegData12
  Register #(.width(32)) Reg12 (.D(WrData), .en(WrReg12), .Q(RegData12), .clk(Clock));  // open: clr
  // Probe on RegData16
  Register #(.width(32)) Reg16 (.D(WrData), .en(WrReg16), .Q(RegData16), .clk(Clock));  // open: clr
  // Probe on RegData20
  Register #(.width(32)) Reg20 (.D(WrData), .en(WrReg20), .Q(RegData20), .clk(Clock));  // open: clr
  // Probe on RegData24
  Register #(.width(32)) Reg24 (.D(WrData), .en(WrReg24), .Q(RegData24), .clk(Clock));  // open: clr
  // Probe on RegData28
  Register #(.width(32)) Reg28 (.D(WrData), .en(WrReg28), .Q(RegData28), .clk(Clock));  // open: clr
  Register #(.width(32)) Reg1 (.D(WrData), .en(WrReg1), .Q(RegData1), .clk(Clock));  // open: clr
  Register #(.width(32)) Reg5 (.D(WrData), .en(WrReg5), .Q(RegData5), .clk(Clock));  // open: clr
  Register #(.width(32)) Reg9 (.D(WrData), .en(WrReg9), .Q(RegData9), .clk(Clock));  // open: clr
  Register #(.width(32)) Reg13 (.D(WrData), .en(WrReg13), .Q(RegData13), .clk(Clock));  // open: clr
  Register #(.width(32)) Reg17 (.D(WrData), .en(WrReg17), .Q(RegData17), .clk(Clock));  // open: clr
  Register #(.width(32)) Reg21 (.D(WrData), .en(WrReg21), .Q(RegData21), .clk(Clock));  // open: clr
  Register #(.width(32)) Reg25 (.D(WrData), .en(WrReg25), .Q(RegData25), .clk(Clock));  // open: clr
  Register #(.width(32)) Reg29 (.D(WrData), .en(WrReg29), .Q(RegData29), .clk(Clock));  // open: clr
  // Probe on RegData1
  // Probe on RegData5
  // Probe on RegData9
  // Probe on RegData13
  // Probe on RegData17
  // Probe on RegData21
  // Probe on RegData25
  // Probe on RegData29
  // Probe on RegData2
  Register #(.width(32)) Reg2 (.D(WrData), .en(WrReg2), .Q(RegData2), .clk(Clock));  // open: clr
  // Probe on RegData6
  Register #(.width(32)) Reg6 (.D(WrData), .en(WrReg6), .Q(RegData6), .clk(Clock));  // open: clr
  // Probe on RegData10
  Register #(.width(32)) Reg10 (.D(WrData), .en(WrReg10), .Q(RegData10), .clk(Clock));  // open: clr
  // Probe on RegData14
  Register #(.width(32)) Reg14 (.D(WrData), .en(WrReg14), .Q(RegData14), .clk(Clock));  // open: clr
  // Probe on RegData18
  Register #(.width(32)) Reg18 (.D(WrData), .en(WrReg18), .Q(RegData18), .clk(Clock));  // open: clr
  // Probe on RegData22
  Register #(.width(32)) Reg22 (.D(WrData), .en(WrReg22), .Q(RegData22), .clk(Clock));  // open: clr
  // Probe on RegData26
  Register #(.width(32)) Reg26 (.D(WrData), .en(WrReg26), .Q(RegData26), .clk(Clock));  // open: clr
  // Probe on RegData30
  Register #(.width(32)) Reg30 (.D(WrData), .en(WrReg30), .Q(RegData30), .clk(Clock));  // open: clr
  // Probe on RegData3
  Register #(.width(32)) Reg3 (.D(WrData), .en(WrReg3), .Q(RegData3), .clk(Clock));  // open: clr
  // Probe on RegData7
  Register #(.width(32)) Reg7 (.D(WrData), .en(WrReg7), .Q(RegData7), .clk(Clock));  // open: clr
  // Probe on RegData11
  Register #(.width(32)) Reg11 (.D(WrData), .en(WrReg11), .Q(RegData11), .clk(Clock));  // open: clr
  // Probe on RegData15
  Register #(.width(32)) Reg15 (.D(WrData), .en(WrReg15), .Q(RegData15), .clk(Clock));  // open: clr
  // Probe on RegData19
  Register #(.width(32)) Reg19 (.D(WrData), .en(WrReg19), .Q(RegData19), .clk(Clock));  // open: clr
  // Probe on RegData23
  Register #(.width(32)) Reg23 (.D(WrData), .en(WrReg23), .Q(RegData23), .clk(Clock));  // open: clr
  // Probe on RegData27
  Register #(.width(32)) Reg27 (.D(WrData), .en(WrReg27), .Q(RegData27), .clk(Clock));  // open: clr
  // Probe on RegData31
  Register #(.width(32)) Reg31 (.D(WrData), .en(WrReg31), .Q(RegData31), .clk(Clock));  // open: clr
  Multiplexer #(.select(5), .width(32), .enable("false")) multiplexer_1 (
    .in0({32{1'b0}}), .in1(RegData1), .in2(RegData2), .in3(RegData3), .in4(RegData4), .in5(RegData5),
    .in6(RegData6), .in7(RegData7), .in8(RegData8), .in9(RegData9), .in10(RegData10), .in11(RegData11),
    .in12(RegData12), .in13(RegData13), .in14(RegData14), .in15(RegData15), .in16(RegData16),
    .in17(RegData17), .in18(RegData18), .in19(RegData19), .in20(RegData20), .in21(RegData21),
    .in22(RegData22), .in23(RegData23), .in24(RegData24), .in25(RegData25), .in26(RegData26),
    .in27(RegData27), .in28(RegData28), .in29(RegData29), .in30(RegData30), .in31(RegData31),
    .out(multiplexer_1_out), .sel(RdAddr1));
  Multiplexer #(.select(5), .width(32), .enable("false")) multiplexer_2 (
    .in0({32{1'b0}}), .in1(RegData1), .in2(RegData2), .in3(RegData3), .in4(RegData4), .in5(RegData5),
    .in6(RegData6), .in7(RegData7), .in8(RegData8), .in9(RegData9), .in10(RegData10), .in11(RegData11),
    .in12(RegData12), .in13(RegData13), .in14(RegData14), .in15(RegData15), .in16(RegData16),
    .in17(RegData17), .in18(RegData18), .in19(RegData19), .in20(RegData20), .in21(RegData21),
    .in22(RegData22), .in23(RegData23), .in24(RegData24), .in25(RegData25), .in26(RegData26),
    .in27(RegData27), .in28(RegData28), .in29(RegData29), .in30(RegData30), .in31(RegData31),
    .out(multiplexer_2_out), .sel(RdAddr2));
  Multiplexer #(.width(32), .enable("false")) multiplexer_3 (
    .in0(multiplexer_1_out), .in1(WrData), .out(RdData1), .sel(and_1_out));
  Comparator #(.width(5), .mode("unsigned")) comparator_1 (
    .a(WrAddr), .b(RdAddr2), .eq(comparator_1_eq));  // open: gt, lt
  Multiplexer #(.width(32), .enable("false")) multiplexer_4 (
    .in0(multiplexer_2_out), .in1(WrData), .out(RdData2), .sel(and_2_out));
  Comparator #(.width(5), .mode("unsigned")) comparator_2 (
    .a(WrAddr), .b(RdAddr1), .eq(comparator_2_eq));  // open: gt, lt
  and and_1 (and_1_out, comparator_2_eq, WrReg, not_1_out);
  and and_2 (and_2_out, comparator_1_eq, WrReg, not_2_out);
  Comparator #(.width(5), .mode("unsigned")) comparator_3 (
    .a(WrAddr), .b({5{1'b0}}), .eq(comparator_3_eq));  // open: gt, lt
  not not_1 (not_1_out, comparator_3_eq);
  Comparator #(.width(5), .mode("unsigned")) comparator_4 (
    .a(WrAddr), .b({5{1'b0}}), .eq(comparator_4_eq));  // open: gt, lt
  not not_2 (not_2_out, comparator_4_eq);
endmodule

module Overflow_Unit (
  input  Add,
  input  Sub,
  input  ASign,
  input  BSign,
  input  ResultSign,
  output Overflow
);

  wire and_1_out, and_2_out, or_1_out, xnor_1_out, xor_1_out, xor_2_out;

  xnor xnor_1 (xnor_1_out, ASign, BSign);
  xor xor_1 (xor_1_out, ASign, BSign);
  and and_1 (and_1_out, xnor_1_out, Add);
  and and_2 (and_2_out, xor_1_out, Sub);
  or or_1 (or_1_out, and_1_out, and_2_out);
  xor xor_2 (xor_2_out, ResultSign, ASign);
  and and_3 (Overflow, or_1_out, xor_2_out);

  // Notes on the sheet:
  //   Overflow occurs when doing addition and sign(A) == sign(B) && sign(result) != sign(A)
  //   Or
  //   Overflow occurs when doing subtraction and sign(A) != sign(B) && sign(result) != sign(A)
endmodule
