// Logisim project MEM_WB.circ as structural Verilog: 1 circuit, main circuit main
module main (
  input  [31:0] in_1,
  input  [31:0] in_2,
  input  [31:0] in_3,
  input  [4:0] in_4,
  input  CLK,
  output out_6,
  output [31:0] out_7,
  output [31:0] out_8,
  output [31:0] out_9,
  output [4:0] out_10
);

  Register #(.width(32)) register_1 (.D(in_1), .Q(out_7), .clk(CLK));  // open: en, clr
  Register #(.width(32)) register_2 (.D(in_2), .Q(out_8), .clk(CLK));  // open: en, clr
  Register #(.width(32)) register_3 (.D(in_3), .Q(out_9), .clk(CLK));  // open: en, clr
  Register #(.width(5)) register_4 (.D(in_4), .Q(out_10), .clk(CLK));  // open: en, clr

  assign out_6 = CLK;

  // Other names for the same wires on the sheet: LW_data[31:0] = in_2; LW_data_Out[31:0] = out_8; PC_4[31:0] = in_1;
  //   PC_4_Out[31:0] = out_7; R_data[31:0] = in_3; R_data_Out[31:0] = out_9; RegDst[4:0] = in_4;
  //   RegDst_Out[4:0] = out_10
endmodule
