// Logisim project PC.circ as structural Verilog: 1 circuit, main circuit main
module main (
  input  in_1,
  input  [31:0] in_2,
  input  in_3,
  output [31:0] out_4
);

  Register #(.width(32)) register_1 (.D(in_2), .en(in_1), .Q(out_4), .clk(in_3));  // open: clr

  // Other names for the same wires on the sheet: Enable = in_1
endmodule
