// Logisim project Sign-extension.circ as structural Verilog: 1 circuit, main circuit main
module main (
  input  [15:0] in_1,
  output [31:0] out_2
);

  Multiplexer #(.width(16)) multiplexer_1 (
    .in0({16{1'b0}}), .in1({16{1'b1}}), .out(out_2[31:16]), .sel(in_1[15]));  // open: en

  assign out_2[15:0] = in_1;

  // Other names for the same wires on the sheet: Instruction_32b[31:0] = {out_2[31:16], in_1};
  //   Instruction__15_0[15:0] = in_1; SignSel = in_1[15]; Ext[15:0] = out_2[31:16]
endmodule
